# Fritzing sketch thermeq3 (saved by Fritzing 0.9.2b)
breadboards: 1

parts:
  Yun = Arduino Yun
  Load_(boiler) = SWITCH-MOMENTARY-2 [package=tactile-switch-1101ne]
  U1 = RELAY [package=relay-t9a]
  LED2 = RGB LED (com. cathode, rgb) [package="5 mm [THT]"]
  R1 = Resistor [tolerance=±5% resistance=220 package="0805 [SMD]"]
  R2 = Resistor [tolerance=±5% resistance=220 package="0805 [SMD]"]
  R3 = Resistor [tolerance=±5% resistance=220 package="0805 [SMD]"]

nets:
  N1: Yun.5V, U1.COIL1
  N2: Yun.D8, R1.Pin_0
  N3: Yun.D9_PWM, R2.Pin_0
  N4: Yun.D10_PWM/SS, U1.COIL2
  N5: Yun.D13/SCK, R3.Pin_0
  N6: Yun.GND, LED2.common_cathode
  N7: Load_(boiler).1, U1.MAIN
  N8: Load_(boiler).2, U1.NO
  N9: LED2.red_anode, R1.Pin_1
  N10: LED2.green_anode, R3.Pin_1
  N11: LED2.blue_anode, R2.Pin_1
